// Logisim project SevenSegDec.circ as structural Verilog: 1 circuit, main circuit SevenSegDec
module SevenSegDec (
  input  A3,
  input  A2,
  input  A1,
  input  A0,
  output S0,
  output S1,
  output S2,
  output S3,
  output S4,
  output S5,
  output S6
);

  wire and_1_out, nor_1_out, not_1_out, not_2_out, not_3_out, not_4_out, or_2_out, or_3_out, or_5_out,
       or_6_out;

  not not_1 (not_1_out, A0);
  or or_1 (S2, not_1_out, A0);
  nor nor_1 (nor_1_out, A0, A2);
  not not_2 (not_2_out, A3);
  and and_1 (and_1_out, A1, nor_1_out);
  or or_2 (or_2_out, A3, A1);
  not not_3 (not_3_out, A0);
  or or_3 (or_3_out, A0, and_1_out);
  or or_4 (S3, or_2_out, not_3_out);
  and and_2 (S1, not_2_out, or_3_out);
  not not_4 (not_4_out, A1);
  or or_5 (or_5_out, A3, A2);
  or or_6 (or_6_out, not_4_out, A0);
  or or_7 (S0, or_5_out, or_6_out);
  _7_Segment_Display u_7_segment_display_1 (.g(S0), .f(S1), .a(S2), .b(S3), .e(S2), .d(S2), .c(S1));  // open: dp

  assign S4 = S2;
  assign S5 = S2;
  assign S6 = S1;

  // Notes on the sheet:
  //   NICOLAS FERTOUT, 260826282
endmodule
