// Logisim project SequentialDivider.circ as structural Verilog: 3 circuits, main circuit Divider
module Divider (
  input  [3:0] Dividend,
  input  [3:0] Divisor,
  input  RESET,
  output [3:0] Remainder,
  output [3:0] Quotient,
  output DONE
);

  wire C_out, for_init_remainder_q, not_1_out, not_2_out, Prevent_shifting_At_First_Iteration_q;
  wire [3:0] shift_register_1_q3;
  wire [7:0] Add_4_zeros_out_2, adder_1_out, bit_extender_1_out, multiplexer_1_out, multiplexer_2_out,
       Shift_Right_out, subtractor_1_out;
  wire [7:4] register_1_q;

  // Probe on Dividend
  // Probe on Divisor
  Clock C (.out(C_out));
  assign bit_extender_1_out = {{4{1'b0}}, Dividend};  // Bit_Extender bit_extender_1
  AddZeros Add_4_zeros (.in_1(Divisor), .out_2(Add_4_zeros_out_2));
  Counter #(.max('h1), .ongoal("stay"), .width(1)) for_init_remainder (
    .Q(for_init_remainder_q), .clk(C_out), .clr(RESET));  // open: load, D, count, carry, up
  Multiplexer #(.enable("false"), .width(8)) multiplexer_1 (
    .in0(bit_extender_1_out), .in1(multiplexer_2_out), .out(multiplexer_1_out), .sel(for_init_remainder_q));
  Counter #(.max('h1), .ongoal("stay"), .width(1)) Prevent_shifting_At_First_Iteration (
    .Q(Prevent_shifting_At_First_Iteration_q), .clk(C_out), .clr(RESET));  // open: load, D, count, carry, up
  Register register_1 (.D(multiplexer_1_out), .en(not_1_out), .clk(C_out), .Q({register_1_q, Remainder}), .clr(RESET));
  Shift_Register Shift_Right (
    .shift(Prevent_shifting_At_First_Iteration_q), .in(1'b0), .clk(C_out), .out(Shift_Right_out[0]),
    .load(RESET), .d0(Add_4_zeros_out_2[7]), .q0(Shift_Right_out[7]), .d1(Add_4_zeros_out_2[6]),
    .q1(Shift_Right_out[6]), .d2(Add_4_zeros_out_2[5]), .q2(Shift_Right_out[5]), .d3(Add_4_zeros_out_2[4]),
    .q3(Shift_Right_out[4]), .d4(Add_4_zeros_out_2[3]), .q4(Shift_Right_out[3]), .d5(Add_4_zeros_out_2[2]),
    .q5(Shift_Right_out[2]), .d6(Add_4_zeros_out_2[1]), .q6(Shift_Right_out[1]), .d7(Add_4_zeros_out_2[0]));  // open: clr, q7
  Subtractor subtractor_1 (
    .a({register_1_q, Remainder}), .b(Shift_Right_out), .out(subtractor_1_out));  // open: bin, bout
  Counter #(.max('h6), .ongoal("stay"), .width(3)) counter_1 (
    .carry(DONE), .clk(C_out), .clr(RESET));  // open: load, D, count, Q, up
  Adder adder_1 (.a(subtractor_1_out), .b(Shift_Right_out), .out(adder_1_out));  // open: cin, cout
  not not_1 (not_1_out, DONE);
  Multiplexer #(.enable("false"), .width(8)) multiplexer_2 (
    .in0(subtractor_1_out), .in1(adder_1_out), .out(multiplexer_2_out), .sel(subtractor_1_out[7]));
  not not_2 (not_2_out, subtractor_1_out[7]);
  Shift_Register #(.length(5)) shift_register_1 (
    .shift(not_1_out), .in(not_2_out), .clk(C_out), .clr(RESET), .q0(shift_register_1_q3[3]),
    .q1(shift_register_1_q3[2]), .q2(shift_register_1_q3[1]), .q3(shift_register_1_q3[0]));  // open: out, load, d0, d1, d2, d3, d4, q4
  // Probe on Remainder
  // Probe on Quotient
  InvertDirection Invert_Direction (.in_1(shift_register_1_q3), .out_2(Quotient));

  // Notes on the sheet:
  //   Nicolas FERTOUT, 260826282
  //   This circuit does not work when the DIVISOR has a most significant bit equal to 1,
  //   because logisim thniks that it is a negative number, and it affects the result of the subtraction.
  //   It still works for positive divisors (since Prof. Hsiu-Chin Lin said they will be no tests for numbers greater than 0111).
  //   It requires 6 iterations (counter stops at 6).
endmodule

module InvertDirection (
  input  [3:0] in_1,
  output [3:0] out_2
);


  assign out_2 = {in_1[0], in_1[1], in_1[2], in_1[3]};
endmodule

module AddZeros (
  input  [3:0] in_1,
  output [7:0] out_2
);


  assign out_2 = {in_1, 4'b0000};
endmodule
