// Logisim project SequentialMultipler.circ as structural Verilog: 2 circuits, main circuit Multiplier
module Multiplier (
  input  [3:0] A_Multriplicand,
  input  [3:0] B_Multiplier,
  input  RESET,
  output [7:0] PRODUCT,
  output DONE
);

  wire C_out, Shift_Right_out;
  wire [7:0] adder_1_out, bit_extender_1_out, Invert_Direction_Again_out_2, Invert_Direction_out_2,
       Shift_left_thanks_to_invertDirection_out;

  Clock C (.out(C_out));
  // Probe on A_Multriplicand
  // Probe on B_Multiplier
  assign bit_extender_1_out = {{4{1'b0}}, A_Multriplicand};  // Bit_Extender bit_extender_1
  Shift_Register #(.length(4)) Shift_Right (
    .in(1'b0), .clk(C_out), .out(Shift_Right_out), .load(RESET), .d0(B_Multiplier[3]), .d1(B_Multiplier[2]),
    .d2(B_Multiplier[1]), .d3(B_Multiplier[0]));  // open: shift, clr, q0, q1, q2, q3
  InvertDirection Invert_Direction (.in_1(bit_extender_1_out), .out_2(Invert_Direction_out_2));
  Shift_Register Shift_left_thanks_to_invertDirection (
    .in(1'b0), .clk(C_out), .out(Shift_left_thanks_to_invertDirection_out[0]), .load(RESET),
    .d0(Invert_Direction_out_2[7]), .q0(Shift_left_thanks_to_invertDirection_out[7]),
    .d1(Invert_Direction_out_2[6]), .q1(Shift_left_thanks_to_invertDirection_out[6]),
    .d2(Invert_Direction_out_2[5]), .q2(Shift_left_thanks_to_invertDirection_out[5]),
    .d3(Invert_Direction_out_2[4]), .q3(Shift_left_thanks_to_invertDirection_out[4]),
    .d4(Invert_Direction_out_2[3]), .q4(Shift_left_thanks_to_invertDirection_out[3]),
    .d5(Invert_Direction_out_2[2]), .q5(Shift_left_thanks_to_invertDirection_out[2]),
    .d6(Invert_Direction_out_2[1]), .q6(Shift_left_thanks_to_invertDirection_out[1]),
    .d7(Invert_Direction_out_2[0]));  // open: shift, clr, q7
  Counter #(.max('h4), .ongoal("stay"), .width(3)) counter_1 (
    .carry(DONE), .clk(C_out), .clr(RESET));  // open: load, D, count, Q, up
  InvertDirection Invert_Direction_Again (
    .in_1(Shift_left_thanks_to_invertDirection_out), .out_2(Invert_Direction_Again_out_2));
  // Probe on Invert_Direction_Again_out_2
  Adder adder_1 (.a(PRODUCT), .b(Invert_Direction_Again_out_2), .out(adder_1_out));  // open: cin, cout
  Register register_1 (.D(adder_1_out), .en(Shift_Right_out), .clk(C_out), .Q(PRODUCT), .clr(RESET));
  // Probe on PRODUCT

  // Notes on the sheet:
  //   Nicolas FERTOUT, 260826282
  //   To simulate a shift left, I invert the input bits,
  //   then shift right, then invert again
endmodule

module InvertDirection (
  input  [7:0] in_1,
  output [7:0] out_2
);


  assign out_2 = {in_1[0], in_1[1], in_1[2], in_1[3], in_1[4], in_1[5], in_1[6], in_1[7]};
endmodule
