// Logisim project led.circ as structural Verilog: 1 circuit, main circuit main
module main (
);

  wire clock_1_out;
  wire [3:0] counter_1_q;
  wire [9:0] rom_1_data;

  Clock clock_1 (.out(clock_1_out));
  Counter #(.max('h9), .width(4)) counter_1 (
    .Q(counter_1_q), .clk(clock_1_out));  // open: load, D, count, carry, up, clr
  ROM #(.addrWidth(4), .dataWidth(10)) rom_1 (.addr(counter_1_q), .data(rom_1_data));
  LED led_1 (.in(rom_1_data[0]));
  LED led_2 (.in(rom_1_data[1]));
  LED led_3 (.in(rom_1_data[3]));
  LED led_4 (.in(rom_1_data[2]));
  LED led_5 (.in(rom_1_data[4]));
  LED led_6 (.in(rom_1_data[5]));
  LED led_7 (.in(rom_1_data[6]));
  LED led_8 (.in(rom_1_data[7]));
  LED led_9 (.in(rom_1_data[8]));
  LED led_10 (.in(rom_1_data[9]));

  // Notes on the sheet:
  //   contents of rom_1 (hex, n*v repeats v):
  //   0 4 40 1 100 4 40 4 100 4
  //   Nicolas FERTOUT, 260826282
  //   First cycle is blank. 
  //   When it reaches the final digit, it comes back to the beginning (blank on the next iteration, and then the 1st digit again).
  //   1
  //   0
  //   3
  //   2
  //   4
  //   5
  //   6
  //   7
  //   8
  //   9
endmodule
